// Logisim project imm-gen.circ as structural Verilog: 1 circuit, main circuit imm_gen
module imm_gen (
  input  [31:0] Instruction,
  input  [2:0] ImmSel,
  output [31:0] Immediate
);

  wire [31:0] BImmediate, IImmediate, JImmediate, SImmediate;

  assign IImmediate = {{20{Instruction[31]}}, Instruction[31:20]};  // Bit_Extender bit_extender_1
  assign BImmediate = {{19{Instruction[31]}}, {Instruction[31], Instruction[7], Instruction[30:25], Instruction[11:8], 1'b0}};  // Bit_Extender bit_extender_2
  assign SImmediate = {{20{Instruction[31]}}, {Instruction[31:25], Instruction[11:7]}};  // Bit_Extender bit_extender_3
  assign JImmediate = {{11{Instruction[31]}}, {Instruction[31], Instruction[19:12], Instruction[20], Instruction[30:21], 1'b0}};  // Bit_Extender bit_extender_4
  Multiplexer #(.select(3), .width(32)) multiplexer_1 (
    .in0(IImmediate), .in1(SImmediate), .in2(BImmediate), .in3({Instruction[31:12], {12{1'b0}}}),
    .in4(JImmediate), .out(Immediate), .sel(ImmSel));  // open: in5, in6, in7

  // Other names for the same wires on the sheet: b_imm_11 = Instruction[7]; s_imm_4[4:0] = Instruction[11:7];
  //   b_imm_4[3:0] = Instruction[11:8]; j_imm_12_19[7:0] = Instruction[19:12]; u_imm_12_31[19:0] = Instruction[31:12];
  //   UImmediate[31:12] = Instruction[31:12]; j_imm_11 = Instruction[20]; j_imm_1_10[9:0] = Instruction[30:21];
  //   b_imm_10_5[5:0] = Instruction[30:25]; s_imm_5_10[5:0] = Instruction[30:25]; b_imm_12 = Instruction[31];
  //   j_imm_20 = Instruction[31]; s_imm_11 = Instruction[31]

  // Notes on the sheet:
  //   INPUTS to your circuit
  //   DON'T CHANGE THE LOCATIONS OF THE INPUTS AND OUTPUTS!
  //   OUTPUT from your circuit
endmodule
