// Logisim project control-logic.circ as structural Verilog: 1 circuit, main circuit control_logic
module control_logic (
  input  [31:0] Instruction,
  input  BrEq,
  input  BrLt,
  output PCSel,
  output RegWEn,
  output [2:0] ImmSel,
  output BrUn,
  output ASel,
  output BSel,
  output [3:0] ALUSel,
  output MemRW,
  output [1:0] WBSel
);

  wire add, addi, and1, and_9_out, and_10_out, and_11_out, and_12_out, and_13_out, and_14_out, and_15_out,
       and_16_out, and_17_out, and_18_out, and_19_out, and_20_out, andi, auipc, beq, bge, bgeu, blt, bltu,
       bne, comparator_1_eq, comparator_1_lt, comparator_2_eq, comparator_3_eq, comparator_4_eq,
       comparator_5_eq, comparator_6_eq, comparator_7_eq, comparator_8_eq, comparator_9_eq, comparator_10_eq,
       comparator_11_eq, comparator_12_eq, comparator_13_eq, comparator_14_eq, comparator_15_eq,
       comparator_16_eq, comparator_17_eq, comparator_17_lt, comparator_18_eq, comparator_19_eq,
       comparator_20_eq, comparator_21_eq, comparator_22_eq, comparator_23_eq, comparator_24_eq,
       comparator_25_eq, comparator_26_eq, comparator_27_eq, comparator_28_eq, comparator_29_eq,
       comparator_30_eq, comparator_31_eq, comparator_32_eq, comparator_33_eq, comparator_34_eq,
       comparator_35_eq, comparator_36_eq, comparator_37_eq, comparator_38_eq, comparator_39_eq,
       comparator_40_eq, comparator_44_eq, comparator_44_lt, comparator_45_eq, comparator_46_eq,
       comparator_47_eq, comparator_48_eq, comparator_49_eq, comparator_50_eq, comparator_51_eq,
       comparator_52_eq, comparator_53_eq, comparator_54_eq, comparator_55_eq, comparator_56_eq,
       comparator_58_lt, comparator_59_eq, comparator_60_eq, is_loadstore, is_store, jal, jalr, lui, mul,
       mulh, mulhu, multiplexer_32_out, multiplexer_33_out, or1, or_9_out, or_10_out, ori, r_f7_00, r_f7_01,
       r_f7_20, sll1, slli, slt1, slti, sra1, srai, srl1, srli, sub, xor1, xori;
  wire [5:0] LoadStoreAddr, LoadStoreBase, LoadStoreFunct3, multiplexer_1_out, multiplexer_2_out,
       multiplexer_3_out, multiplexer_4_out, multiplexer_5_out, multiplexer_6_out, multiplexer_7_out,
       multiplexer_8_out, multiplexer_9_out, multiplexer_10_out, multiplexer_11_out, multiplexer_12_out,
       multiplexer_13_out, multiplexer_14_out, multiplexer_15_out, multiplexer_16_out, multiplexer_17_out,
       multiplexer_18_out, multiplexer_19_out, multiplexer_20_out, multiplexer_21_out, multiplexer_22_out,
       multiplexer_23_out, multiplexer_24_out, multiplexer_25_out, multiplexer_26_out, multiplexer_27_out,
       multiplexer_28_out, multiplexer_29_out, multiplexer_30_out, multiplexer_31_out, or_3_out, or_4_out,
       or_6_out, ROM_B, ROM_I, ROM_JU, ROM_NonMem, ROM_R, RomAddrFinal;
  wire [15:14] rom_1_data;

  Multiplexer #(.width(6)) multiplexer_1 (.in0({6{1'b0}}), .in1(6'b010111), .out(multiplexer_1_out), .sel(add));
  Multiplexer #(.width(6)) multiplexer_2 (.in0({6{1'b0}}), .in1(6'b011000), .out(multiplexer_2_out), .sel(sub));
  Multiplexer #(.width(6)) multiplexer_3 (.in0({6{1'b0}}), .in1(6'b011001), .out(multiplexer_3_out), .sel(and1));
  Multiplexer #(.width(6)) multiplexer_4 (.in0({6{1'b0}}), .in1(6'b011010), .out(multiplexer_4_out), .sel(or1));
  Multiplexer #(.width(6)) multiplexer_5 (.in0({6{1'b0}}), .in1(6'b011011), .out(multiplexer_5_out), .sel(xor1));
  Multiplexer #(.width(6)) multiplexer_6 (.in0({6{1'b0}}), .in1(6'b011100), .out(multiplexer_6_out), .sel(sll1));
  Multiplexer #(.width(6)) multiplexer_7 (.in0({6{1'b0}}), .in1(6'b011101), .out(multiplexer_7_out), .sel(srl1));
  Multiplexer #(.width(6)) multiplexer_8 (.in0({6{1'b0}}), .in1(6'b011110), .out(multiplexer_8_out), .sel(sra1));
  Multiplexer #(.width(6)) multiplexer_9 (.in0({6{1'b0}}), .in1(6'b011111), .out(multiplexer_9_out), .sel(slt1));
  Multiplexer #(.width(6)) multiplexer_10 (.in0({6{1'b0}}), .in1(6'b100000), .out(multiplexer_10_out), .sel(mul));
  Multiplexer #(.width(6)) multiplexer_11 (.in0({6{1'b0}}), .in1(6'b100001), .out(multiplexer_11_out), .sel(mulh));
  Multiplexer #(.width(6)) multiplexer_12 (.in0({6{1'b0}}), .in1(6'b100010), .out(multiplexer_12_out), .sel(mulhu));
  Multiplexer #(.width(6)) multiplexer_13 (.in0({6{1'b0}}), .in1(6'b100011), .out(multiplexer_13_out), .sel(beq));
  Multiplexer #(.width(6)) multiplexer_14 (.in0({6{1'b0}}), .in1(6'b100100), .out(multiplexer_14_out), .sel(bge));
  Multiplexer #(.width(6)) multiplexer_15 (.in0({6{1'b0}}), .in1(6'b100101), .out(multiplexer_15_out), .sel(bgeu));
  Multiplexer #(.width(6)) multiplexer_16 (.in0({6{1'b0}}), .in1(6'b100110), .out(multiplexer_16_out), .sel(blt));
  Multiplexer #(.width(6)) multiplexer_17 (.in0({6{1'b0}}), .in1(6'b100111), .out(multiplexer_17_out), .sel(bltu));
  Multiplexer #(.width(6)) multiplexer_18 (.in0({6{1'b0}}), .in1(6'b101000), .out(multiplexer_18_out), .sel(bne));
  ROM #(.addrWidth(6), .dataWidth(16)) rom_1 (
    .addr(RomAddrFinal), .data({rom_1_data, WBSel, MemRW, ALUSel, BSel, ASel, BrUn, ImmSel, RegWEn}));
  Comparator #(.width(7)) comparator_1 (
    .a(Instruction[6:0]), .b(7'b0010011), .eq(comparator_1_eq), .lt(comparator_1_lt));  // open: gt
  Comparator #(.width(3)) comparator_2 (.a(Instruction[14:12]), .b(3'b000), .eq(comparator_2_eq));  // open: gt, lt
  Comparator #(.width(7)) comparator_3 (.a(Instruction[6:0]), .b(7'b0010011), .eq(comparator_3_eq));  // open: gt, lt
  Comparator #(.width(3)) comparator_4 (.a(Instruction[14:12]), .b(3'b001), .eq(comparator_4_eq));  // open: gt, lt
  Comparator #(.width(7)) comparator_5 (.a(Instruction[6:0]), .b(7'b0010011), .eq(comparator_5_eq));  // open: gt, lt
  Comparator #(.width(3)) comparator_6 (.a(Instruction[14:12]), .b(3'b010), .eq(comparator_6_eq));  // open: gt, lt
  Comparator #(.width(7)) comparator_7 (.a(Instruction[6:0]), .b(7'b0010011), .eq(comparator_7_eq));  // open: gt, lt
  Comparator #(.width(3)) comparator_8 (.a(Instruction[14:12]), .b(3'b100), .eq(comparator_8_eq));  // open: gt, lt
  Comparator #(.width(7)) comparator_9 (.a(Instruction[6:0]), .b(7'b0010011), .eq(comparator_9_eq));  // open: gt, lt
  Comparator #(.width(3)) comparator_10 (.a(Instruction[14:12]), .b(3'b101), .eq(comparator_10_eq));  // open: gt, lt
  Comparator #(.width(7)) comparator_11 (.a(Instruction[6:0]), .b(7'b0010011), .eq(comparator_11_eq));  // open: gt, lt
  Comparator #(.width(3)) comparator_12 (.a(Instruction[14:12]), .b(3'b101), .eq(comparator_12_eq));  // open: gt, lt
  Comparator #(.width(7)) comparator_13 (.a(Instruction[6:0]), .b(7'b0010011), .eq(comparator_13_eq));  // open: gt, lt
  Comparator #(.width(3)) comparator_14 (.a(Instruction[14:12]), .b(3'b110), .eq(comparator_14_eq));  // open: gt, lt
  Comparator #(.width(7)) comparator_15 (.a(Instruction[6:0]), .b(7'b0010011), .eq(comparator_15_eq));  // open: gt, lt
  Comparator #(.width(3)) comparator_16 (.a(Instruction[14:12]), .b(3'b111), .eq(comparator_16_eq));  // open: gt, lt
  assign ROM_B = multiplexer_13_out | multiplexer_14_out | multiplexer_15_out | multiplexer_16_out | multiplexer_17_out | multiplexer_18_out;  // OR_Gate or_1, 6 bits wide
  and and_1 (addi, comparator_1_eq, comparator_2_eq);
  and and_2 (slli, comparator_3_eq, comparator_4_eq);
  and and_3 (slti, comparator_5_eq, comparator_6_eq);
  and and_4 (xori, comparator_7_eq, comparator_8_eq);
  and and_5 (srli, comparator_9_eq, comparator_10_eq);
  and and_6 (srai, comparator_11_eq, comparator_12_eq);
  and and_7 (ori, comparator_13_eq, comparator_14_eq);
  and and_8 (andi, comparator_15_eq, comparator_16_eq);
  assign ROM_R = multiplexer_1_out | multiplexer_2_out | multiplexer_3_out | multiplexer_4_out | multiplexer_5_out | multiplexer_6_out | multiplexer_7_out | multiplexer_8_out | multiplexer_9_out | multiplexer_10_out | multiplexer_11_out | multiplexer_12_out;  // OR_Gate or_2, 6 bits wide
  Multiplexer #(.width(6)) multiplexer_19 (.in0({6{1'b0}}), .in1(6'b111101), .out(multiplexer_19_out), .sel(auipc));
  Multiplexer #(.width(6)) multiplexer_20 (.in0({6{1'b0}}), .in1(6'b001111), .out(multiplexer_20_out), .sel(addi));
  Multiplexer #(.width(6)) multiplexer_21 (.in0({6{1'b0}}), .in1(6'b010000), .out(multiplexer_21_out), .sel(slli));
  Multiplexer #(.width(6)) multiplexer_22 (.in0({6{1'b0}}), .in1(6'b010001), .out(multiplexer_22_out), .sel(slti));
  Multiplexer #(.width(6)) multiplexer_23 (.in0({6{1'b0}}), .in1(6'b010010), .out(multiplexer_23_out), .sel(xori));
  Multiplexer #(.width(6)) multiplexer_24 (.in0({6{1'b0}}), .in1(6'b010011), .out(multiplexer_24_out), .sel(srli));
  Multiplexer #(.width(6)) multiplexer_25 (
    .in0(multiplexer_24_out), .in1(multiplexer_26_out), .out(multiplexer_25_out), .sel(Instruction[30]));
  Multiplexer #(.width(6)) multiplexer_26 (.in0({6{1'b0}}), .in1(6'b010100), .out(multiplexer_26_out), .sel(srai));
  Multiplexer #(.width(6)) multiplexer_27 (.in0({6{1'b0}}), .in1(6'b010101), .out(multiplexer_27_out), .sel(ori));
  Multiplexer #(.width(6)) multiplexer_28 (.in0({6{1'b0}}), .in1(6'b010110), .out(multiplexer_28_out), .sel(andi));
  Multiplexer #(.width(6)) multiplexer_29 (.in0({6{1'b0}}), .in1(6'b111011), .out(multiplexer_29_out), .sel(jal));
  Multiplexer #(.width(6)) multiplexer_30 (.in0({6{1'b0}}), .in1(6'b111100), .out(multiplexer_30_out), .sel(jalr));
  Multiplexer #(.width(6)) multiplexer_31 (.in0({6{1'b0}}), .in1(6'b111110), .out(multiplexer_31_out), .sel(lui));
  Comparator #(.width(7)) comparator_17 (
    .a(Instruction[6:0]), .b(7'b0110011), .eq(comparator_17_eq), .lt(comparator_17_lt));  // open: gt
  Comparator #(.width(3)) comparator_18 (.a(Instruction[14:12]), .b(3'b000), .eq(comparator_18_eq));  // open: gt, lt
  Comparator #(.width(7)) comparator_19 (.a(Instruction[6:0]), .b(7'b0110011), .eq(comparator_19_eq));  // open: gt, lt
  Comparator #(.width(3)) comparator_20 (.a(Instruction[14:12]), .b(3'b000), .eq(comparator_20_eq));  // open: gt, lt
  Comparator #(.width(7)) comparator_21 (.a(Instruction[6:0]), .b(7'b0110011), .eq(comparator_21_eq));  // open: gt, lt
  Comparator #(.width(3)) comparator_22 (.a(Instruction[14:12]), .b(3'b111), .eq(comparator_22_eq));  // open: gt, lt
  Comparator #(.width(7)) comparator_23 (.a(Instruction[6:0]), .b(7'b0110011), .eq(comparator_23_eq));  // open: gt, lt
  Comparator #(.width(3)) comparator_24 (.a(Instruction[14:12]), .b(3'b110), .eq(comparator_24_eq));  // open: gt, lt
  Comparator #(.width(7)) comparator_25 (.a(Instruction[6:0]), .b(7'b0110011), .eq(comparator_25_eq));  // open: gt, lt
  Comparator #(.width(3)) comparator_26 (.a(Instruction[14:12]), .b(3'b100), .eq(comparator_26_eq));  // open: gt, lt
  Comparator #(.width(7)) comparator_27 (.a(Instruction[6:0]), .b(7'b0110011), .eq(comparator_27_eq));  // open: gt, lt
  Comparator #(.width(3)) comparator_28 (.a(Instruction[14:12]), .b(3'b001), .eq(comparator_28_eq));  // open: gt, lt
  Comparator #(.width(7)) comparator_29 (.a(Instruction[6:0]), .b(7'b0110011), .eq(comparator_29_eq));  // open: gt, lt
  Comparator #(.width(3)) comparator_30 (.a(Instruction[14:12]), .b(3'b101), .eq(comparator_30_eq));  // open: gt, lt
  Comparator #(.width(7)) comparator_31 (.a(Instruction[6:0]), .b(7'b0110011), .eq(comparator_31_eq));  // open: gt, lt
  Comparator #(.width(3)) comparator_32 (.a(Instruction[14:12]), .b(3'b101), .eq(comparator_32_eq));  // open: gt, lt
  Comparator #(.width(7)) comparator_33 (.a(Instruction[6:0]), .b(7'b0110011), .eq(comparator_33_eq));  // open: gt, lt
  Comparator #(.width(3)) comparator_34 (.a(Instruction[14:12]), .b(3'b010), .eq(comparator_34_eq));  // open: gt, lt
  Comparator #(.width(7)) comparator_35 (.a(Instruction[6:0]), .b(7'b0110011), .eq(comparator_35_eq));  // open: gt, lt
  Comparator #(.width(3)) comparator_36 (.a(Instruction[14:12]), .b(3'b000), .eq(comparator_36_eq));  // open: gt, lt
  Comparator #(.width(7)) comparator_37 (.a(Instruction[6:0]), .b(7'b0110011), .eq(comparator_37_eq));  // open: gt, lt
  Comparator #(.width(3)) comparator_38 (.a(Instruction[14:12]), .b(3'b001), .eq(comparator_38_eq));  // open: gt, lt
  Comparator #(.width(7)) comparator_39 (.a(Instruction[6:0]), .b(7'b0110011), .eq(comparator_39_eq));  // open: gt, lt
  Comparator #(.width(3)) comparator_40 (.a(Instruction[14:12]), .b(3'b011), .eq(comparator_40_eq));  // open: gt, lt
  assign or_3_out = multiplexer_20_out | multiplexer_21_out | multiplexer_22_out | multiplexer_23_out;  // OR_Gate or_3, 6 bits wide
  assign or_4_out = multiplexer_27_out | multiplexer_28_out;  // OR_Gate or_4, 6 bits wide
  assign ROM_JU = multiplexer_29_out | multiplexer_30_out | multiplexer_19_out | multiplexer_31_out;  // OR_Gate or_5, 6 bits wide
  assign or_6_out = multiplexer_25_out | or_4_out;  // OR_Gate or_6, 6 bits wide
  assign ROM_NonMem = ROM_I | ROM_R | ROM_B | ROM_JU;  // OR_Gate or_7, 6 bits wide
  and and_9 (and_9_out, comparator_17_eq, comparator_18_eq);
  and and_10 (and_10_out, comparator_19_eq, comparator_20_eq);
  and and_11 (and_11_out, comparator_21_eq, comparator_22_eq);
  and and_12 (and_12_out, comparator_23_eq, comparator_24_eq);
  and and_13 (and_13_out, comparator_25_eq, comparator_26_eq);
  and and_14 (and_14_out, comparator_27_eq, comparator_28_eq);
  and and_15 (and_15_out, comparator_29_eq, comparator_30_eq);
  and and_16 (and_16_out, comparator_31_eq, comparator_32_eq);
  and and_17 (and_17_out, comparator_33_eq, comparator_34_eq);
  and and_18 (and_18_out, comparator_35_eq, comparator_36_eq);
  and and_19 (and_19_out, comparator_37_eq, comparator_38_eq);
  and and_20 (and_20_out, comparator_39_eq, comparator_40_eq);
  assign ROM_I = or_3_out | or_6_out;  // OR_Gate or_8, 6 bits wide
  and and_21 (add, and_9_out, r_f7_00);
  and and_22 (sub, and_10_out, r_f7_20);
  and and_23 (and1, and_11_out, r_f7_00);
  and and_24 (or1, and_12_out, r_f7_00);
  and and_25 (xor1, and_13_out, r_f7_00);
  and and_26 (sll1, and_14_out, r_f7_00);
  and and_27 (srl1, and_15_out, r_f7_00);
  and and_28 (sra1, and_16_out, r_f7_20);
  and and_29 (slt1, and_17_out, r_f7_00);
  and and_30 (mul, and_18_out, r_f7_01);
  and and_31 (mulh, and_19_out, r_f7_01);
  and and_32 (mulhu, and_20_out, r_f7_01);
  or or_9 (or_9_out, bge, bgeu);
  or or_10 (or_10_out, blt, bltu);
  Multiplexer multiplexer_32 (.in0(bne), .in1(beq), .out(multiplexer_32_out), .sel(BrEq));
  Multiplexer multiplexer_33 (.in0(or_9_out), .in1(or_10_out), .out(multiplexer_33_out), .sel(BrLt));
  Multiplexer #(.width(6)) multiplexer_34 (.in0(6'b110000), .in1(6'b111000), .out(LoadStoreBase), .sel(is_store));
  Comparator #(.width(7)) comparator_41 (.a(Instruction[31:25]), .b({7{1'b0}}), .eq(r_f7_00));  // open: gt, lt
  Comparator #(.width(7)) comparator_42 (.a(Instruction[31:25]), .b(7'b0100000), .eq(r_f7_20));  // open: gt, lt
  Comparator #(.width(7)) comparator_43 (.a(Instruction[31:25]), .b(7'b0000001), .eq(r_f7_01));  // open: gt, lt
  Comparator #(.width(7)) comparator_44 (
    .a(Instruction[6:0]), .b(7'b1100011), .eq(comparator_44_eq), .lt(comparator_44_lt));  // open: gt
  Comparator #(.width(3)) comparator_45 (.a(Instruction[14:12]), .b(3'b000), .eq(comparator_45_eq));  // open: gt, lt
  Comparator #(.width(7)) comparator_46 (.a(Instruction[6:0]), .b(7'b1100011), .eq(comparator_46_eq));  // open: gt, lt
  Comparator #(.width(3)) comparator_47 (.a(Instruction[14:12]), .b(3'b101), .eq(comparator_47_eq));  // open: gt, lt
  Comparator #(.width(7)) comparator_48 (.a(Instruction[6:0]), .b(7'b1100011), .eq(comparator_48_eq));  // open: gt, lt
  Comparator #(.width(3)) comparator_49 (.a(Instruction[14:12]), .b(3'b111), .eq(comparator_49_eq));  // open: gt, lt
  Comparator #(.width(7)) comparator_50 (.a(Instruction[6:0]), .b(7'b1100011), .eq(comparator_50_eq));  // open: gt, lt
  Comparator #(.width(3)) comparator_51 (.a(Instruction[14:12]), .b(3'b100), .eq(comparator_51_eq));  // open: gt, lt
  Comparator #(.width(7)) comparator_52 (.a(Instruction[6:0]), .b(7'b1100011), .eq(comparator_52_eq));  // open: gt, lt
  Comparator #(.width(3)) comparator_53 (.a(Instruction[14:12]), .b(3'b110), .eq(comparator_53_eq));  // open: gt, lt
  Comparator #(.width(7)) comparator_54 (.a(Instruction[6:0]), .b(7'b1100011), .eq(comparator_54_eq));  // open: gt, lt
  Comparator #(.width(3)) comparator_55 (.a(Instruction[14:12]), .b(3'b001), .eq(comparator_55_eq));  // open: gt, lt
  Comparator #(.width(7)) comparator_56 (.a(Instruction[6:0]), .b(7'b0000011), .eq(comparator_56_eq));  // open: gt, lt
  Comparator #(.width(7)) comparator_57 (.a(Instruction[6:0]), .b(7'b0100011), .eq(is_store));  // open: gt, lt
  assign LoadStoreFunct3 = {{3{1'b0}}, Instruction[14:12]};  // Bit_Extender bit_extender_1
  Multiplexer #(.width(6)) multiplexer_35 (
    .in0(ROM_NonMem), .in1(LoadStoreAddr), .out(RomAddrFinal), .sel(is_loadstore));
  or or_11 (PCSel, multiplexer_32_out, multiplexer_33_out, jal, jalr);
  and and_33 (beq, comparator_44_eq, comparator_45_eq);
  and and_34 (bge, comparator_46_eq, comparator_47_eq);
  and and_35 (bgeu, comparator_48_eq, comparator_49_eq);
  and and_36 (blt, comparator_50_eq, comparator_51_eq);
  and and_37 (bltu, comparator_52_eq, comparator_53_eq);
  and and_38 (bne, comparator_54_eq, comparator_55_eq);
  or or_12 (is_loadstore, comparator_56_eq, is_store);
  assign LoadStoreAddr = LoadStoreBase | LoadStoreFunct3;  // OR_Gate or_13, 6 bits wide
  Comparator #(.width(7)) comparator_58 (
    .a(Instruction[6:0]), .b(7'b1101111), .eq(jal), .lt(comparator_58_lt));  // open: gt
  Comparator #(.width(7)) comparator_59 (.a(Instruction[6:0]), .b(7'b1100111), .eq(comparator_59_eq));  // open: gt, lt
  Comparator #(.width(3)) comparator_60 (.a(Instruction[14:12]), .b(3'b000), .eq(comparator_60_eq));  // open: gt, lt
  Comparator #(.width(7)) comparator_61 (.a(Instruction[6:0]), .b(7'b0010111), .eq(auipc));  // open: gt, lt
  Comparator #(.width(7)) comparator_62 (.a(Instruction[6:0]), .b(7'b0110111), .eq(lui));  // open: gt, lt
  and and_39 (jalr, comparator_59_eq, comparator_60_eq);

  // Other names for the same wires on the sheet: opcode[6:0] = Instruction[6:0]; funct3[2:0] = Instruction[14:12];
  //   fun7[6:0] = Instruction[31:25]; LorA = Instruction[30]

  // Notes on the sheet:
  //   INPUTS to your circuit
  //   Connect ROM Input here ->
  //   contents of rom_1 (hex, n*v repeats v):
  //   15*0 1041 10c1 1141 1241 12c1 16c1 1341 13c1 1001 1601 1381 1301 1201 1081 1281 1681 1101 1401 1481
  //   1581 64 64 74 64 74 64 7*0 2041 2041 2041 5*0 842 842 842 3069 3041 1067 17c7
  //   ROM FOR CONTROL LOGIC
  //   DON'T CHANGE THE LOCATIONS OF THE INPUTS AND OUTPUTS!
  //   This is only if you choose to do the ROM option
  //   CONNECT
  //   WIRE
  //   TO
  //   USE
  //   ROM
  //   OUTPUT from your circuit
  //   Reminder: If using ROM, use combinational logic for PCSel
endmodule
