// Logisim project partial-store.circ as structural Verilog: 1 circuit, main circuit partial_store
module partial_store (
  input  [31:0] Instruction,
  input  [31:0] MemAddress,
  input  [31:0] DataFromReg,
  input  MemRW,
  output [3:0] MemWriteMask,
  output [31:0] DataToMem
);

  wire [3:0] multiplexer_5_out, multiplexer_6_out, multiplexer_7_out;
  wire [31:0] a0, a01, a1, a2, a3, a12, a23, bit_extender_2_out, bit_extender_3_out, bit_extender_4_out,
       bit_extender_6_out, bit_extender_7_out, multiplexer_1_out, multiplexer_2_out, multiplexer_3_out;

  assign a0 = {{24{1'b0}}, DataFromReg[7:0]};  // Bit_Extender bit_extender_1
  assign bit_extender_2_out = {{24{1'b0}}, DataFromReg[7:0]};  // Bit_Extender bit_extender_2
  assign bit_extender_3_out = {{24{1'b0}}, DataFromReg[7:0]};  // Bit_Extender bit_extender_3
  assign bit_extender_4_out = {{24{1'b0}}, DataFromReg[7:0]};  // Bit_Extender bit_extender_4
  assign a01 = {{16{1'b0}}, DataFromReg[15:0]};  // Bit_Extender bit_extender_5
  assign bit_extender_6_out = {{16{1'b0}}, DataFromReg[15:0]};  // Bit_Extender bit_extender_6
  assign bit_extender_7_out = {{16{1'b0}}, DataFromReg[15:0]};  // Bit_Extender bit_extender_7
  Shifter #(.width(32)) shifter_1 (.in(bit_extender_2_out), .\dist (5'b01000), .out(a1));
  Multiplexer #(.select(2), .width(32)) multiplexer_1 (
    .in0(a0), .in1(a1), .in2(a2), .in3(a3), .out(multiplexer_1_out), .sel(MemAddress[1:0]));
  Multiplexer #(.select(2), .width(32)) multiplexer_2 (
    .in0(a01), .in1(a12), .in2(a23), .out(multiplexer_2_out), .sel(MemAddress[1:0]));  // open: in3
  Shifter #(.width(32)) shifter_2 (.in(bit_extender_3_out), .\dist (5'b10000), .out(a2));
  Shifter #(.width(32)) shifter_3 (.in(bit_extender_4_out), .\dist (5'b11000), .out(a3));
  Shifter #(.width(32)) shifter_4 (.in(bit_extender_6_out), .\dist (5'b10000), .out(a23));
  Shifter #(.width(32)) shifter_5 (.in(bit_extender_7_out), .\dist (5'b01000), .out(a12));
  Multiplexer #(.select(2), .width(32)) multiplexer_3 (
    .in0(multiplexer_1_out), .in1(multiplexer_2_out), .in2(DataFromReg), .out(multiplexer_3_out),
    .sel(Instruction[13:12]));  // open: in3
  Multiplexer #(.width(32)) multiplexer_4 (.in0({32{1'b0}}), .in1(multiplexer_3_out), .out(DataToMem), .sel(MemRW));
  Multiplexer #(.select(2), .width(4)) multiplexer_5 (
    .in0(4'b0001), .in1(4'b0010), .in2(4'b0100), .in3(4'b1000), .out(multiplexer_5_out), .sel(MemAddress[1:0]));
  Multiplexer #(.select(2), .width(4)) multiplexer_6 (
    .in0(4'b0011), .in1(4'b0110), .in2(4'b1100), .out(multiplexer_6_out), .sel(MemAddress[1:0]));  // open: in3
  Multiplexer #(.select(2), .width(4)) multiplexer_7 (
    .in0(multiplexer_5_out), .in1(multiplexer_6_out), .in2(4'b1111), .out(multiplexer_7_out),
    .sel(Instruction[13:12]));  // open: in3
  Multiplexer #(.width(4)) multiplexer_8 (.in0(4'b0000), .in1(multiplexer_7_out), .out(MemWriteMask), .sel(MemRW));

  // Other names for the same wires on the sheet: opcode[6:0] = Instruction[6:0]; myfunct3[1:0] = Instruction[13:12];
  //   low2[1:0] = MemAddress[1:0]

  // Notes on the sheet:
  //   INPUTS to your circuit
  //   DON'T CHANGE THE LOCATIONS OF THE INPUTS AND OUTPUTS!
  //   OUTPUT from your circuit
endmodule
