// Logisim project regfile.circ as structural Verilog: 1 circuit, main circuit regfile
module regfile (
  input  [4:0] ReadIndex1,
  input  [4:0] ReadIndex2,
  input  [4:0] WriteIndex,
  input  [31:0] WriteData,
  input  RegWEn,
  input  clk,
  output [31:0] ra,
  output [31:0] sp,
  output [31:0] t0,
  output [31:0] t1,
  output [31:0] t2,
  output [31:0] s0,
  output [31:0] s1,
  output [31:0] a0,
  output [31:0] ReadData1,
  output [31:0] ReadData2
);

  wire we1, we2, we3, we4, we5, we6, we7, we8, we9, we10, we11, we12, we13, we14, we15, we16, we17, we18,
       we19, we20, we21, we22, we23, we24, we25, we26, we27, we28, we29, we30, we31;
  wire [31:0] r3, r4, r11, r12, r13, r14, r15, r16, r17, r18, r19, r20, r21, r22, r23, r24, r25, r26, r27,
       r28, r29, r30, r31;

  Decoder #(.enable("true"), .select(5)) decoder_1 (
    .out1(we1), .out2(we2), .out3(we3), .out4(we4), .out5(we5), .out6(we6), .out7(we7), .out8(we8),
    .out9(we9), .out10(we10), .out11(we11), .out12(we12), .out13(we13), .out14(we14), .out15(we15),
    .out16(we16), .out17(we17), .out18(we18), .out19(we19), .out20(we20), .out21(we21), .out22(we22),
    .out23(we23), .out24(we24), .out25(we25), .out26(we26), .out27(we27), .out28(we28), .out29(we29),
    .out30(we30), .out31(we31), .sel(WriteIndex), .en(RegWEn));  // open: out0
  Register #(.width(32)) x1 (.D(WriteData), .en(we1), .clk(clk), .Q(ra), .clr(1'b0));
  Register #(.width(32)) x5 (.D(WriteData), .en(we5), .clk(clk), .Q(t0), .clr(1'b0));
  Register #(.width(32)) x9 (.D(WriteData), .en(we9), .clk(clk), .Q(s1), .clr(1'b0));
  Register #(.width(32)) x13 (.D(WriteData), .en(we13), .clk(clk), .Q(r13), .clr(1'b0));
  Register #(.width(32)) x17 (.D(WriteData), .en(we17), .clk(clk), .Q(r17), .clr(1'b0));
  Register #(.width(32)) x21 (.D(WriteData), .en(we21), .clk(clk), .Q(r21), .clr(1'b0));
  Register #(.width(32)) x25 (.D(WriteData), .en(we25), .clk(clk), .Q(r25), .clr(1'b0));
  Register #(.width(32)) x29 (.D(WriteData), .en(we29), .clk(clk), .Q(r29), .clr(1'b0));
  Register #(.width(32)) x2 (.D(WriteData), .en(we2), .clk(clk), .Q(sp), .clr(1'b0));
  Register #(.width(32)) x6 (.D(WriteData), .en(we6), .clk(clk), .Q(t1), .clr(1'b0));
  Register #(.width(32)) x10 (.D(WriteData), .en(we10), .clk(clk), .Q(a0), .clr(1'b0));
  Register #(.width(32)) x14 (.D(WriteData), .en(we14), .clk(clk), .Q(r14), .clr(1'b0));
  Register #(.width(32)) x18 (.D(WriteData), .en(we18), .clk(clk), .Q(r18), .clr(1'b0));
  Register #(.width(32)) x22 (.D(WriteData), .en(we22), .clk(clk), .Q(r22), .clr(1'b0));
  Register #(.width(32)) x26 (.D(WriteData), .en(we26), .clk(clk), .Q(r26), .clr(1'b0));
  Register #(.width(32)) x30 (.D(WriteData), .en(we30), .clk(clk), .Q(r30), .clr(1'b0));
  Register #(.width(32)) x3 (.D(WriteData), .en(we3), .clk(clk), .Q(r3), .clr(1'b0));
  Register #(.width(32)) x7 (.D(WriteData), .en(we7), .clk(clk), .Q(t2), .clr(1'b0));
  Register #(.width(32)) x11 (.D(WriteData), .en(we11), .clk(clk), .Q(r11), .clr(1'b0));
  Register #(.width(32)) x15 (.D(WriteData), .en(we15), .clk(clk), .Q(r15), .clr(1'b0));
  Register #(.width(32)) x19 (.D(WriteData), .en(we19), .clk(clk), .Q(r19), .clr(1'b0));
  Register #(.width(32)) x23 (.D(WriteData), .en(we23), .clk(clk), .Q(r23), .clr(1'b0));
  Register #(.width(32)) x27 (.D(WriteData), .en(we27), .clk(clk), .Q(r27), .clr(1'b0));
  Register #(.width(32)) x31 (.D(WriteData), .en(we31), .clk(clk), .Q(r31), .clr(1'b0));
  Register #(.width(32)) x4 (.D(WriteData), .en(we4), .clk(clk), .Q(r4), .clr(1'b0));
  Register #(.width(32)) x8 (.D(WriteData), .en(we8), .clk(clk), .Q(s0), .clr(1'b0));
  Register #(.width(32)) x12 (.D(WriteData), .en(we12), .clk(clk), .Q(r12), .clr(1'b0));
  Register #(.width(32)) x16 (.D(WriteData), .en(we16), .clk(clk), .Q(r16), .clr(1'b0));
  Register #(.width(32)) x20 (.D(WriteData), .en(we20), .clk(clk), .Q(r20), .clr(1'b0));
  Register #(.width(32)) x24 (.D(WriteData), .en(we24), .clk(clk), .Q(r24), .clr(1'b0));
  Register #(.width(32)) x28 (.D(WriteData), .en(we28), .clk(clk), .Q(r28), .clr(1'b0));
  Multiplexer #(.select(5), .width(32)) multiplexer_1 (
    .in0({32{1'b0}}), .in1(ra), .in2(sp), .in3(r3), .in4(r4), .in5(t0), .in6(t1), .in7(t2), .in8(s0),
    .in9(s1), .in10(a0), .in11(r11), .in12(r12), .in13(r13), .in14(r14), .in15(r15), .in16(r16), .in17(r17),
    .in18(r18), .in19(r19), .in20(r20), .in21(r21), .in22(r22), .in23(r23), .in24(r24), .in25(r25),
    .in26(r26), .in27(r27), .in28(r28), .in29(r29), .in30(r30), .in31(r31), .out(ReadData1), .sel(ReadIndex1));
  Multiplexer #(.select(5), .width(32)) multiplexer_2 (
    .in0({32{1'b0}}), .in1(ra), .in2(sp), .in3(r3), .in4(r4), .in5(t0), .in6(t1), .in7(t2), .in8(s0),
    .in9(s1), .in10(a0), .in11(r11), .in12(r12), .in13(r13), .in14(r14), .in15(r15), .in16(r16), .in17(r17),
    .in18(r18), .in19(r19), .in20(r20), .in21(r21), .in22(r22), .in23(r23), .in24(r24), .in25(r25),
    .in26(r26), .in27(r27), .in28(r28), .in29(r29), .in30(r30), .in31(r31), .out(ReadData2), .sel(ReadIndex2));

  // Notes on the sheet:
  //   INPUTS to your circuit
  //   x0 = 0
  //   DON'T CHANGE THE LOCATIONS OF THE INPUTS AND OUTPUTS!
  //   These are DEBUG/TEST outputs from your circuit.
  //   OUTPUTS from your circuit
endmodule
